# Fritzing sketch circuit figurines (saved by Fritzing 1.0.2b)
perfboards: 2

parts:
  S1 = Reed switch [package=THT]
  R1 = Resistor [tolerance=±5% power=0.25W resistance=1k package=THT]
  S2 = Reed switch [package=THT]
  R2 = Resistor [tolerance=±5% power=0.25W resistance=1k package=THT]
  S3 = Reed switch [package=THT]
  R3 = Resistor [tolerance=±5% power=0.25W resistance=1k package=THT]
  S4 = Reed switch [package=THT]
  R4 = Resistor [tolerance=±5% power=0.25W resistance=1k package=THT]
  Part1 = Arduino Uno (Rev3)  # not connected
  JP1 = Header 2 [package=molex-1x2_lock]  # not connected
  JP2 = Header 2 [package=molex-1x2_lock]
  JP3 = Header 2 [package=molex-1x2_lock]  # not connected
  JP4 = Header 2 [package=molex-1x2_lock]  # not connected
  JP5 = Header 1 [package=1x01_offset]  # not connected
  JP6 = Header 1 [package=1x01_offset]  # not connected
  JP7 = Header 1 [package=1x01_offset]  # not connected
  JP8 = Header 1 [package=1x01_offset]  # not connected
  JP9 = Header 1 [package=1x01_offset]  # not connected
  JP10 = Header 1 [package=1x01_offset]  # not connected
  JP11 = Header 1 [package=1x01_offset]  # not connected
  JP19 = Header 2 [package=molex-1x2_lock]  # not connected
  JP20 = Header 2 [package=molex-1x2_lock]  # not connected
  JP21 = Header 2 [package=molex-1x2_lock]  # not connected
  JP22 = Header 2 [package=molex-1x2_lock]  # not connected
  R6 = Vertical Resistor [tolerance=±5% resistance=1k package=THT]  # not connected
  R7 = Vertical Resistor [tolerance=±5% resistance=1k package=THT]  # not connected
  R8 = Vertical Resistor [tolerance=±5% resistance=1k package=THT]  # not connected
  R9 = Vertical Resistor [tolerance=±5% resistance=1k package=THT]  # not connected
  J1 = male pin header, 4 pins [form="♂ (male)"]  # not connected
  J2 = male pin header, 3 pins [form="♂ (male)"]  # not connected

nets:
  5V: S1.pin_1, S2.pin_1, S3.pin_1, S4.pin_1, JP2.1
  IO 1: S1.pin_2, R1.Pin_0, JP2.2
  GND: R1.Pin_1, R2.Pin_1, R3.Pin_1, R4.Pin_1
  IO 2: S2.pin_2, R2.Pin_0
  IO 3: S3.pin_2, R3.Pin_0
  IO 4: S4.pin_2, R4.Pin_0

notes:
  5V
  Ground
  Souder sur le dessus --->

custom parts:
  Vertical Resistor: A generic resistor (0.25W)
